# Fritzing sketch lamp (saved by Fritzing 0.9.4)
breadboards: 1

parts:
  LED1-10 = LED - 5mm [color="White (4500K)" package="5 mm [THT]"]  # not connected
  LED2 = LED - 5mm [color="White (4500K)" package="5 mm [THT]"]  # not connected
  LED3 = LED - 5mm [color="White (4500K)" package="5 mm [THT]"]  # not connected
  LED4 = LED - 5mm [color="White (4500K)" package="5 mm [THT]"]  # not connected
  LED5 = LED - 5mm [color="White (4500K)" package="5 mm [THT]"]  # not connected
  LED6 = LED - 5mm [color="White (4500K)" package="5 mm [THT]"]  # not connected
  LED7 = LED - 5mm [color="White (4500K)" package="5 mm [THT]"]
  LED8 = LED - 5mm [color="White (4500K)" package="5 mm [THT]"]  # not connected
  LED9 = LED - 5mm [color="White (4500K)" package="5 mm [THT]"]  # not connected
  LED10 = LED - 5mm [color="White (4500K)" package="5 mm [THT]"]
  LED11 = LED - 5mm [color="White (4500K)" package="5 mm [THT]"]  # not connected
  LED12 = LED - 5mm [color="White (4500K)" package="5 mm [THT]"]  # not connected
  LED13 = LED - 5mm [color="White (4500K)" package="5 mm [THT]"]  # not connected
  LED14 = LED - 5mm [color="White (4500K)" package="5 mm [THT]"]
  LED15 = LED - 5mm [color="White (4500K)" package="5 mm [THT]"]
  LED16 = LED - 5mm [color="White (4500K)" package="5 mm [THT]"]  # not connected
  LED11-20_(stem) = LED - 5mm [color="White (4500K)" package="5 mm [THT]"]  # not connected
  LED17 = LED - 5mm [color="White (4500K)" package="5 mm [THT]"]  # not connected
  LED18 = LED - 5mm [color="White (4500K)" package="5 mm [THT]"]  # not connected
  LED19 = LED - 5mm [color="White (4500K)" package="5 mm [THT]"]  # not connected
  Arduino_1 = Arduino Uno (Rev3)
  Shade_pulse_freq = Rotary Potentiometer (Small) [maximum_resistance=100kΩ package=THT]
  R2 = Rotary Potentiometer (Small) [maximum_resistance=100kΩ package=THT]
  S1 = Toggle Switch [package=THT]

nets:
  N1: LED7.cathode, LED10.cathode, LED14.cathode, LED15.cathode, S1.L1
  N2: LED7.anode, LED10.anode, Arduino_1.D8
  N3: LED14.anode, LED15.anode, Arduino_1.D11_PWM/MOSI
  N4: Arduino_1.A0, Shade_pulse_freq.wiper
  N5: Arduino_1.A1, R2.wiper
  N6: Arduino_1.GND, Shade_pulse_freq.leg1, R2.leg1, S1.COM
  N7: Arduino_1.5V, Shade_pulse_freq.leg2
